# Fritzing sketch Wiring (saved by Fritzing 0.9.3b)
circuit board: 8.46667cm x 5.64444cm
breadboards: 1

parts:
  R1 = Resistor [tolerance=±5% resistance=220 package=THT]
  R2 = Resistor [tolerance=±5% resistance=220 package=THT]
  R3 = Resistor [tolerance=±5% resistance=220 package=THT]
  LED1 = RGB LED - (4 legs) [package="5 mm [THT]"]
  U1 = LCD-16X2 [package=lcd-16x2_noholes]
  Part1 = Thumb Joystick
  Part2 = Arduino Uno (Rev3)
  R4 = Trimmer Potentiometer [maximum_resistance=10kΩ package=THT]

nets:
  N1: R1.Pin_0, LED1.red_cathode
  N2: R1.Pin_1, Part2.D11_PWM/MOSI
  N3: R2.Pin_0, LED1.green_cathode
  N4: R2.Pin_1, Part2.D10_PWM/SS
  N5: R3.Pin_0, LED1.blue_cathode
  N6: R3.Pin_1, Part2.D9_PWM
  GND: LED1.common_anode, U1.VSS, U1.K, Part1.GND, Part2.GND, R4.leg2
  VDD: U1.VDD, U1.A, Part1.VCC, Part2.5V, R4.leg1
  N7: U1.VO, R4.wiper
  N8: U1.RS, Part2.D12/MISO
  N9: U1.R_W, Part2.D13/SCK
  N10: U1.DB4, Part2.D4
  N11: U1.DB5, Part2.D5_PWM
  N12: U1.DB6, Part2.D6_PWM
  N13: U1.DB7, Part2.D7
  N14: Part1.SEL, Part2.D2
  N15: Part1.HORZ, Part2.A0
  N16: Part1.VERT, Part2.A1
